// Logisim project EElab.circ as structural Verilog: 10 circuits, main circuit main
module main (
  output [3:0] out_1,
  output [3:0] out_2
);

  wire and_1_out, and_2_out, and_6_out, and_9_out, and_13_out, and_16_out, and_17_out, and_18_out,
       and_19_out, B7, B7_out, B8, B8_out, B9, B9_out, B12, B12_out, B13, B13_out, B14, B14_out, B17,
       B17_out, B18, B18_out, B19, B19_out, CLK, cnt_signal, D7, D8, D9, D12, D13, D14, D17, D18, D19,
       d_ff_1_q, d_ff_2_q, d_ff_3_q, d_ff_4_q, d_ff_5_q, d_ff_6_q, d_ff_7_q, d_ff_8_q, d_ff_9_q, d_ff_10_q,
       d_ff_11_q, d_ff_12_q, d_ff_13_q, d_ff_14_q, d_ff_15_q, d_ff_16_q, d_ff_17_q, d_ff_18_q, d_ff_19_q,
       d_ff_20_q, demultiplexer_1_out0, demultiplexer_1_out1, demultiplexer_1_out2, demultiplexer_1_out3,
       demultiplexer_1_out8, demultiplexer_1_out9, demultiplexer_1_out10, demultiplexer_1_out11,
       demultiplexer_1_out12, demultiplexer_1_out13, demultiplexer_1_out14, demultiplexer_1_out15, en, G7,
       G8, G9, G12, G13, G14, G17, G18, G19, GG, not_1_out, not_2_out, not_3_out, not_4_out, not_5_out,
       not_6_out, not_7_out, not_8_out, not_9_out, not_10_out, not_11_out, not_12_out, not_13_out,
       not_14_out, not_15_out, not_16_out, not_17_out, not_18_out, not_19_out, or_1_out, or_2_out, or_3_out,
       or_4_out, or_5_out, or_6_out, or_7_out, or_8_out, or_9_out, R7, R8, R9, R12, R13, R14, R17, R18, R19,
       register_1_q, register_2_q, register_3_q, register_4_q, register_5_q, register_6_q, register_7_q,
       register_8_q, register_9_q, rst, xor_1_out, xor_2_out, xor_3_out, xor_4_out, xor_5_out, xor_6_out,
       xor_7_out, xor_8_out, xor_9_out;
  wire [3:0] cnt1, cnt2;
  wire [4:0] fire_1_out_2, fire_1_out_3, fire_1_out_4, fire_1_out_5, fire_1_out_6, fire_2_out_2,
       fire_2_out_3, fire_2_out_4, fire_2_out_5, fire_2_out_6, fire_3_out_2, fire_3_out_3, fire_3_out_4,
       fire_3_out_5, fire_3_out_6, fire_top_1_out_2, fire_top_1_out_3, fire_top_1_out_4, fire_top_1_out_5,
       fire_top_1_out_6, fire_top_2_out_2, fire_top_2_out_3, fire_top_2_out_4, fire_top_2_out_5,
       fire_top_2_out_6, fire_top_3_out_2, fire_top_3_out_3, fire_top_3_out_4, fire_top_3_out_5,
       fire_top_3_out_6, S7, S8, S9, S12, S13, S14, S17, S18, S19;
  wire [10:0] gg_1_out_2, gg_1_out_3, gg_1_out_4, gg_1_out_5, gg_1_out_6, gg_1_out_7, gg_1_out_8, gg_1_out_9,
       gg_1_out_10, gg_1_out_11, gg_1_out_12;
  wire [14:0] right_1_out_4, right_1_out_5, right_1_out_6, right_1_out_7, right_2_out_4, right_2_out_5,
       right_2_out_6, right_2_out_7;

  Clock clock_1 (.out(CLK));
  or or_1 (or_1_out, B12, B17, B18);
  or or_2 (or_2_out, B7, B12, B17, B13);
  or or_3 (or_3_out, B12, B7, B8);
  state state_1 (.out(G17), .B(or_1_out), .rst(rst), .R(R17), .clk(CLK));
  state state_2 (.out(G12), .B(or_2_out), .rst(rst), .R(R12), .clk(CLK));
  state state_3 (.out(G7), .B(or_3_out), .rst(rst), .R(R7), .clk(CLK));
  DotMatrix #(.matrixcols(11), .matrixrows(11)) dotmatrix_1 (
    .col0(gg_1_out_7), .col1(gg_1_out_2), .col2(gg_1_out_8), .col3(gg_1_out_3), .col4(gg_1_out_9),
    .col5(gg_1_out_4), .col6(gg_1_out_10), .col7(gg_1_out_5), .col8(gg_1_out_11), .col9(gg_1_out_6),
    .col10(gg_1_out_12));
  GG gg_1 (
    .out_7(gg_1_out_7), .out_2(gg_1_out_2), .out_8(gg_1_out_8), .out_3(gg_1_out_3), .out_9(gg_1_out_9),
    .out_4(gg_1_out_4), .out_10(gg_1_out_10), .out_5(gg_1_out_5), .out_11(gg_1_out_11), .out_6(gg_1_out_6),
    .out_12(gg_1_out_12), .GG(GG));
  right right_1 (
    .B2(B12), .B1(B7), .B3(B17), .out_4(right_1_out_4), .out_5(right_1_out_5), .out_6(right_1_out_6),
    .out_7(right_1_out_7));
  DotMatrix #(.matrixrows(5)) dotmatrix_2 (
    .col0(fire_top_1_out_6), .col1(fire_top_1_out_5), .col2(fire_top_1_out_4), .col3(fire_top_1_out_3),
    .col4(fire_top_1_out_2));
  DotMatrix #(.matrixrows(5)) dotmatrix_3 (.col0(S17), .col1(S17), .col2(S17), .col3(S17), .col4(S17));
  DotMatrix #(.matrixrows(5)) dotmatrix_4 (.col0(S12), .col1(S12), .col2(S12), .col3(S12), .col4(S12));
  DotMatrix #(.matrixrows(5)) dotmatrix_5 (.col0(S7), .col1(S7), .col2(S7), .col3(S7), .col4(S7));
  DotMatrix #(.matrixrows(15)) dotmatrix_6 (
    .col0(right_1_out_4), .col1(right_1_out_5), .col2(right_1_out_6), .col3(right_1_out_7));  // open: col4
  DotMatrix #(.matrixrows(5)) dotmatrix_7 (
    .col0(fire_1_out_2), .col1(fire_1_out_3), .col2(fire_1_out_4), .col3(fire_1_out_5), .col4(fire_1_out_6));
  Fire fire_1 (
    .out_2(fire_1_out_2), .out_3(fire_1_out_3), .out_4(fire_1_out_4), .out_5(fire_1_out_5),
    .out_6(fire_1_out_6), .B(B7));
  or or_4 (or_4_out, B19, B17, B18, B13);
  or or_5 (or_5_out, B18, B12, B13, B14, B8);
  or or_6 (or_6_out, B13, B8, B9, B7);
  Fire_top fire_top_1 (
    .out_2(fire_top_1_out_2), .out_3(fire_top_1_out_3), .out_4(fire_top_1_out_4), .out_5(fire_top_1_out_5),
    .out_6(fire_top_1_out_6), .B(B17));
  Fire_top fire_top_2 (
    .out_2(fire_top_2_out_2), .out_3(fire_top_2_out_3), .out_4(fire_top_2_out_4), .out_5(fire_top_2_out_5),
    .out_6(fire_top_2_out_6), .B(B18));
  DotMatrix #(.matrixrows(5)) dotmatrix_8 (
    .col0(fire_top_2_out_6), .col1(fire_top_2_out_5), .col2(fire_top_2_out_4), .col3(fire_top_2_out_3),
    .col4(fire_top_2_out_2));
  DotMatrix #(.matrixrows(5)) dotmatrix_9 (.col0(S18), .col1(S18), .col2(S18), .col3(S18), .col4(S18));
  DotMatrix #(.matrixrows(5)) dotmatrix_10 (.col0(S13), .col1(S13), .col2(S13), .col3(S13), .col4(S13));
  DotMatrix #(.matrixrows(5)) dotmatrix_11 (.col0(S8), .col1(S8), .col2(S8), .col3(S8), .col4(S8));
  DotMatrix #(.matrixrows(5)) dotmatrix_12 (
    .col0(fire_2_out_2), .col1(fire_2_out_3), .col2(fire_2_out_4), .col3(fire_2_out_5), .col4(fire_2_out_6));
  Fire fire_2 (
    .out_2(fire_2_out_2), .out_3(fire_2_out_3), .out_4(fire_2_out_4), .out_5(fire_2_out_5),
    .out_6(fire_2_out_6), .B(B8));
  state state_4 (.out(G18), .B(or_4_out), .rst(rst), .R(R18), .clk(CLK));
  state state_5 (.out(G13), .B(or_5_out), .rst(rst), .R(R13), .clk(CLK));
  state state_6 (.out(G8), .B(or_6_out), .rst(rst), .R(R8), .clk(CLK));
  Fire_top fire_top_3 (
    .out_2(fire_top_3_out_2), .out_3(fire_top_3_out_3), .out_4(fire_top_3_out_4), .out_5(fire_top_3_out_5),
    .out_6(fire_top_3_out_6), .B(B19));
  DotMatrix #(.matrixrows(5)) dotmatrix_13 (
    .col0(fire_top_3_out_6), .col1(fire_top_3_out_5), .col2(fire_top_3_out_4), .col3(fire_top_3_out_3),
    .col4(fire_top_3_out_2));
  DotMatrix #(.matrixrows(5)) dotmatrix_14 (.col0(S19), .col1(S19), .col2(S19), .col3(S19), .col4(S19));
  DotMatrix #(.matrixrows(5)) dotmatrix_15 (.col0(S14), .col1(S14), .col2(S14), .col3(S14), .col4(S14));
  DotMatrix #(.matrixrows(5)) dotmatrix_16 (.col0(S9), .col1(S9), .col2(S9), .col3(S9), .col4(S9));
  DotMatrix #(.matrixrows(15)) dotmatrix_17 (
    .col1(right_2_out_7), .col2(right_2_out_6), .col3(right_2_out_5), .col4(right_2_out_4));  // open: col0
  DotMatrix #(.matrixrows(5)) dotmatrix_18 (
    .col0(fire_3_out_2), .col1(fire_3_out_3), .col2(fire_3_out_4), .col3(fire_3_out_5), .col4(fire_3_out_6));
  Fire fire_3 (
    .out_2(fire_3_out_2), .out_3(fire_3_out_3), .out_4(fire_3_out_4), .out_5(fire_3_out_5),
    .out_6(fire_3_out_6), .B(B9));
  Hex_Digit_Display hex_digit_display_1 (.value(cnt1));  // open: dp
  Hex_Digit_Display hex_digit_display_2 (.value(cnt2));  // open: dp
  right right_2 (
    .B2(B14), .B1(B9), .B3(B19), .out_4(right_2_out_4), .out_5(right_2_out_5), .out_6(right_2_out_6),
    .out_7(right_2_out_7));
  or or_7 (or_7_out, B14, B19, B18);
  or or_8 (or_8_out, B13, B19, B14, B9);
  or or_9 (or_9_out, B9, B14, B8);
  not not_1 (not_1_out, d_ff_2_q);
  and and_1 (and_1_out, d_ff_1_q, not_1_out);
  state state_7 (.out(G19), .B(or_7_out), .rst(rst), .R(R19), .clk(CLK));
  state state_8 (.out(G14), .B(or_8_out), .rst(rst), .R(R14), .clk(CLK));
  state state_9 (.out(G9), .B(or_9_out), .rst(rst), .R(R9), .clk(CLK));
  D_Flip_Flop d_ff_1 (.clk(CLK), .D(G17), .Q(d_ff_1_q));  // open: Qn, preset, en, reset
  D_Flip_Flop d_ff_2 (.clk(CLK), .D(d_ff_1_q), .Q(d_ff_2_q));  // open: Qn, preset, en, reset
  and and_2 (and_2_out, d_ff_3_q, not_2_out);
  and and_3 (B17, B17_out, G17);
  Button u_B17 (.out(B17_out));
  Button u_B12 (.out(B12_out));
  Button u_B7 (.out(B7_out));
  D_Flip_Flop d_ff_3 (.clk(CLK), .D(G18), .Q(d_ff_3_q));  // open: Qn, preset, en, reset
  D_Flip_Flop d_ff_4 (.clk(CLK), .D(d_ff_3_q), .Q(d_ff_4_q));  // open: Qn, preset, en, reset
  not not_2 (not_2_out, d_ff_4_q);
  and and_4 (B18, B18_out, G18);
  and and_5 (B19, B19_out, G19);
  Button u_B18 (.out(B18_out));
  Button u_B19 (.out(B19_out));
  Button u_B14 (.out(B14_out));
  Button u_B13 (.out(B13_out));
  Button u_B8 (.out(B8_out));
  Button u_B9 (.out(B9_out));
  or or_10 (D13, demultiplexer_1_out0, demultiplexer_1_out1, demultiplexer_1_out2, demultiplexer_1_out3);
  Counter counter_1 (.D({cnt2, cnt1}), .Q({cnt2, cnt1}), .clk(cnt_signal), .clr(rst));  // open: load, count, carry
  not not_3 (not_3_out, G18);
  not not_4 (not_4_out, G17);
  D_Flip_Flop d_ff_5 (.clk(CLK), .D(G19), .Q(d_ff_5_q));  // open: Qn, preset, en, reset
  D_Flip_Flop d_ff_6 (.clk(CLK), .D(d_ff_5_q), .Q(d_ff_6_q));  // open: Qn, preset, en, reset
  not not_5 (not_5_out, d_ff_6_q);
  and and_6 (and_6_out, d_ff_5_q, not_5_out);
  and and_7 (B12, B12_out, G12);
  and and_8 (B13, B13_out, G13);
  Random #(.width(4), .trigger("falling")) random_1 (.clk(CLK), .next(1'b1), .out(out_1));  // open: clr
  Demultiplexer #(.select(4)) demultiplexer_1 (
    .out0(demultiplexer_1_out0), .out1(demultiplexer_1_out1), .out2(demultiplexer_1_out2),
    .out3(demultiplexer_1_out3), .out4(D7), .out5(D19), .out6(D9), .out7(D17), .out8(demultiplexer_1_out8),
    .out9(demultiplexer_1_out9), .out10(demultiplexer_1_out10), .out11(demultiplexer_1_out11),
    .out12(demultiplexer_1_out12), .out13(demultiplexer_1_out13), .out14(demultiplexer_1_out14),
    .out15(demultiplexer_1_out15), .in(1'b1), .sel(out_2), .en(rst));
  or or_11 (D18, demultiplexer_1_out10, demultiplexer_1_out11);
  or or_12 (D8, demultiplexer_1_out8, demultiplexer_1_out9);
  not not_6 (not_6_out, G19);
  not not_7 (not_7_out, G12);
  D_Flip_Flop d_ff_7 (.clk(CLK), .D(G12), .Q(d_ff_7_q));  // open: Qn, preset, en, reset
  D_Flip_Flop d_ff_8 (.clk(CLK), .D(d_ff_7_q), .Q(d_ff_8_q));  // open: Qn, preset, en, reset
  not not_8 (not_8_out, d_ff_8_q);
  and and_9 (and_9_out, d_ff_7_q, not_8_out);
  and and_10 (B14, B14_out, G14);
  and and_11 (B7, B7_out, G7);
  Register #(.width(4)) u_rst (.D(out_1), .Q(out_2), .clk(rst));  // open: en, clr
  or or_13 (D14, demultiplexer_1_out14, demultiplexer_1_out15);
  or or_14 (D12, demultiplexer_1_out12, demultiplexer_1_out13);
  and and_12 (GG, not_4_out, not_3_out, not_6_out, not_7_out, not_10_out, not_9_out, not_13_out, not_12_out, not_15_out);
  not not_9 (not_9_out, G14);
  not not_10 (not_10_out, G13);
  D_Flip_Flop d_ff_9 (.clk(CLK), .D(G13), .Q(d_ff_9_q));  // open: Qn, preset, en, reset
  D_Flip_Flop d_ff_10 (.clk(CLK), .D(d_ff_9_q), .Q(d_ff_10_q));  // open: Qn, preset, en, reset
  not not_11 (not_11_out, d_ff_10_q);
  and and_13 (and_13_out, d_ff_9_q, not_11_out);
  or or_15 (cnt_signal, and_1_out, and_2_out, and_6_out, and_9_out, and_13_out, and_16_out, and_17_out, and_18_out, and_19_out);
  and and_14 (B8, B8_out, G8);
  and and_15 (B9, B9_out, G9);
  not not_12 (not_12_out, G8);
  not not_13 (not_13_out, G7);
  D_Flip_Flop d_ff_11 (.clk(CLK), .D(G14), .Q(d_ff_11_q));  // open: Qn, preset, en, reset
  D_Flip_Flop d_ff_12 (.clk(CLK), .D(d_ff_11_q), .Q(d_ff_12_q));  // open: Qn, preset, en, reset
  not not_14 (not_14_out, d_ff_12_q);
  and and_16 (and_16_out, d_ff_11_q, not_14_out);
  Button rst_2 (.out(rst));
  Register #(.width(1), .trigger("high")) register_1 (.D(D7), .Q(register_1_q), .clk(en));  // open: en, clr
  Register #(.width(1), .trigger("high")) register_2 (.D(D8), .Q(register_2_q), .clk(en));  // open: en, clr
  Register #(.width(1), .trigger("high")) register_3 (.D(D9), .Q(register_3_q), .clk(en));  // open: en, clr
  Register #(.width(1), .trigger("high")) register_4 (.D(D12), .Q(register_4_q), .clk(en));  // open: en, clr
  Register #(.width(1), .trigger("high")) register_5 (.D(D13), .Q(register_5_q), .clk(en));  // open: en, clr
  Register #(.width(1), .trigger("high")) register_6 (.D(D14), .Q(register_6_q), .clk(en));  // open: en, clr
  Register #(.width(1), .trigger("high")) register_7 (.D(D17), .Q(register_7_q), .clk(en));  // open: en, clr
  Register #(.width(1), .trigger("high")) register_8 (.D(D18), .Q(register_8_q), .clk(en));  // open: en, clr
  Register #(.width(1), .trigger("high")) register_9 (.D(D19), .Q(register_9_q), .clk(en));  // open: en, clr
  not not_15 (not_15_out, G9);
  D_Flip_Flop d_ff_13 (.clk(CLK), .D(G7), .Q(d_ff_13_q));  // open: Qn, preset, en, reset
  D_Flip_Flop d_ff_14 (.clk(CLK), .D(d_ff_13_q), .Q(d_ff_14_q));  // open: Qn, preset, en, reset
  not not_16 (not_16_out, d_ff_14_q);
  and and_17 (and_17_out, d_ff_13_q, not_16_out);
  D_Flip_Flop d_ff_15 (.clk(CLK), .D(rst), .Q(d_ff_15_q));  // open: Qn, preset, en, reset
  D_Flip_Flop d_ff_16 (.clk(CLK), .D(G8), .Q(d_ff_16_q));  // open: Qn, preset, en, reset
  D_Flip_Flop d_ff_17 (.clk(CLK), .D(d_ff_16_q), .Q(d_ff_17_q));  // open: Qn, preset, en, reset
  not not_17 (not_17_out, d_ff_17_q);
  and and_18 (and_18_out, d_ff_16_q, not_17_out);
  D_Flip_Flop d_ff_18 (.clk(CLK), .D(d_ff_15_q), .Q(d_ff_18_q));  // open: Qn, preset, en, reset
  not not_18 (not_18_out, d_ff_18_q);
  xor xor_1 (xor_1_out, rst, register_1_q);
  xor xor_2 (xor_2_out, rst, register_2_q);
  xor xor_3 (xor_3_out, rst, register_3_q);
  xor xor_4 (xor_4_out, rst, register_4_q);
  xor xor_5 (xor_5_out, rst, register_5_q);
  xor xor_6 (xor_6_out, rst, register_6_q);
  xor xor_7 (xor_7_out, rst, register_7_q);
  xor xor_8 (xor_8_out, rst, register_8_q);
  xor xor_9 (xor_9_out, rst, register_9_q);
  not not_19 (not_19_out, d_ff_20_q);
  and and_19 (and_19_out, d_ff_19_q, not_19_out);
  and and_20 (en, not_18_out, d_ff_15_q);
  and and_21 (R7, rst, xor_1_out);
  and and_22 (R8, rst, xor_2_out);
  and and_23 (R9, rst, xor_3_out);
  and and_24 (R12, rst, xor_4_out);
  and and_25 (R13, rst, xor_5_out);
  and and_26 (R14, rst, xor_6_out);
  and and_27 (R17, rst, xor_7_out);
  and and_28 (R18, rst, xor_8_out);
  and and_29 (R19, rst, xor_9_out);
  D_Flip_Flop d_ff_19 (.clk(CLK), .D(G9), .Q(d_ff_19_q));  // open: Qn, preset, en, reset
  D_Flip_Flop d_ff_20 (.clk(CLK), .D(d_ff_19_q), .Q(d_ff_20_q));  // open: Qn, preset, en, reset
  Multiplexer #(.width(5)) multiplexer_1 (.in0({5{1'b0}}), .in1({5{1'b1}}), .out(S17), .sel(G17));  // open: en
  Multiplexer #(.width(5)) multiplexer_2 (.in0({5{1'b0}}), .in1({5{1'b1}}), .out(S13), .sel(G13));  // open: en
  Multiplexer #(.width(5)) multiplexer_3 (.in0({5{1'b0}}), .in1({5{1'b1}}), .out(S7), .sel(G7));  // open: en
  Multiplexer #(.width(5)) multiplexer_4 (.in0({5{1'b0}}), .in1({5{1'b1}}), .out(S19), .sel(G19));  // open: en
  Multiplexer #(.width(5)) multiplexer_5 (.in0({5{1'b0}}), .in1({5{1'b1}}), .out(S14), .sel(G14));  // open: en
  Multiplexer #(.width(5)) multiplexer_6 (.in0({5{1'b0}}), .in1({5{1'b1}}), .out(S8), .sel(G8));  // open: en
  Multiplexer #(.width(5)) multiplexer_7 (.in0({5{1'b0}}), .in1({5{1'b1}}), .out(S9), .sel(G9));  // open: en
  Multiplexer #(.width(5)) multiplexer_8 (.in0({5{1'b0}}), .in1({5{1'b1}}), .out(S12), .sel(G12));  // open: en
  Multiplexer #(.width(5)) multiplexer_9 (.in0({5{1'b0}}), .in1({5{1'b1}}), .out(S18), .sel(G18));  // open: en

  // Other names for the same wires on the sheet: S3 = B8; S4 = B9; S10 = B9; S2 = B7; S6 = B7; S11 = B12; S15 = B14;
  //   S16 = B17; S22 = B17; S23 = B18; S20 = B19; S24 = B19; SELECT[3:0] = out_2
endmodule

module button (
  input  rst,
  output [2:0] out_2,
  output [2:0] out_3,
  output out_4,
  output out_5,
  output out_6,
  output out_7,
  output out_8,
  output out_9,
  output out_10,
  output out_11,
  output out_12,
  output out_13
);

  wire adder_1_out, adder_2_out, adder_3_out, adder_4_out, adder_5_out, adder_6_out, adder_7_out,
       adder_8_out, adder_9_out, B7_2_out, B8_out, B9_2_out, B12_2_out, B13_out, B14_2_out, B17_2_out,
       B18_out, B19_2_out, clock_1_out, demultiplexer_1_out0, demultiplexer_1_out1, demultiplexer_1_out2,
       or_1_out, or_2_out, or_3_out, or_4_out, or_5_out, or_6_out, or_7_out, or_8_out, or_9_out, rst_out,
       undriven, undriven_2, undriven_3, undriven_4, undriven_5, undriven_6;
  wire [4:0] B13;

  Adder #(.width(1)) adder_1 (.a(out_4), .b(1'b0), .out(adder_1_out), .cin(1'b1));  // open: cout
  Register #(.width(1)) B17 (.D(adder_1_out), .Q(out_4), .clk(or_1_out), .clr(demultiplexer_1_out2));  // open: en
  or or_1 (or_1_out, B12_2_out, B17_2_out, B18_out);
  Button B17_2 (.out(B17_2_out));
  Adder #(.width(1)) adder_2 (.a(out_7), .b(1'b0), .out(adder_2_out), .cin(1'b1));  // open: cout
  Register #(.width(1)) B12 (.D(adder_2_out), .Q(out_7), .clk(or_2_out), .clr(undriven));  // open: en
  or or_2 (or_2_out, B17_2_out, B12_2_out, B7_2_out, B13_out);
  Button B12_2 (.out(B12_2_out));
  Adder #(.width(1)) adder_3 (.a(out_10), .b(1'b0), .out(adder_3_out), .cin(1'b1));  // open: cout
  Register #(.width(1)) B7 (.D(adder_3_out), .Q(out_10), .clk(or_3_out), .clr(undriven_2));  // open: en
  or or_3 (or_3_out, B12_2_out, B7_2_out, B8_out);
  Button B7_2 (.out(B7_2_out));
  Adder #(.width(1)) adder_4 (.a(out_5), .b(1'b0), .out(adder_4_out), .cin(1'b1));  // open: cout
  or or_4 (or_4_out, B17_2_out, B13_out, B18_out, B19_2_out);
  Button B18 (.out(B18_out));
  Adder #(.width(1)) adder_5 (.a(out_8), .b(1'b0), .out(adder_5_out), .cin(1'b1));  // open: cout
  or or_5 (or_5_out, B12_2_out, B18_out, B13_out, B8_out, B14_2_out);
  Button u_B13 (.out(B13_out));
  Adder #(.width(1)) adder_6 (.a(out_11), .b(1'b0), .out(adder_6_out), .cin(1'b1));  // open: cout
  or or_6 (or_6_out, B7_2_out, B13_out, B8_out, B9_2_out);
  Button B8 (.out(B8_out));
  Register #(.width(1)) B18_2 (.D(adder_4_out), .Q(out_5), .clk(or_4_out), .clr(demultiplexer_1_out1));  // open: en
  Register #(.width(1)) B13_2 (.D(adder_5_out), .Q(out_8), .clk(or_5_out), .clr(undriven_3));  // open: en
  Register #(.width(1)) B8_2 (.D(adder_6_out), .Q(out_11), .clk(or_6_out), .clr(undriven_4));  // open: en
  Register #(.width(1)) B19 (.D(adder_7_out), .Q(out_6), .clk(or_7_out), .clr(demultiplexer_1_out0));  // open: en
  Adder #(.width(1)) adder_7 (.a(out_6), .b(1'b0), .out(adder_7_out), .cin(1'b1));  // open: cout
  or or_7 (or_7_out, B18_out, B14_2_out, B19_2_out);
  Button B19_2 (.out(B19_2_out));
  Adder #(.width(1)) adder_8 (.a(out_9), .b(1'b0), .out(adder_8_out), .cin(1'b1));  // open: cout
  Register #(.width(1)) B14 (.D(adder_8_out), .Q(out_9), .clk(or_8_out), .clr(undriven_5));  // open: en
  or or_8 (or_8_out, B13_out, B14_2_out, B9_2_out, B19_2_out);
  Button B14_2 (.out(B14_2_out));
  Adder #(.width(1)) adder_9 (.a(out_12), .b(1'b0), .out(adder_9_out), .cin(1'b1));  // open: cout
  Register #(.width(1)) B9 (.D(adder_9_out), .Q(out_12), .clk(or_9_out), .clr(undriven_6));  // open: en
  or or_9 (or_9_out, B14_2_out, B8_out, B9_2_out);
  Button B9_2 (.out(B9_2_out));
  Clock clock_1 (.out(clock_1_out));
  Random #(.width(3), .trigger("falling")) random_1 (.clk(clock_1_out), .next(1'b1), .out(out_2));  // open: clr
  Button u_rst (.out(rst_out));
  Demultiplexer #(.select(3)) demultiplexer_1 (
    .out0(demultiplexer_1_out0), .out1(demultiplexer_1_out1), .out2(demultiplexer_1_out2));  // open: out3, out4, out5, out6, out7, in, sel, en
  Register #(.width(3)) rst_2 (.D(out_2), .Q(out_3), .clk(rst_out));  // open: en, clr
  Multiplexer #(.width(5)) multiplexer_1 (.in0({5{1'b1}}), .in1({5{1'b0}}), .out(B13), .sel(out_13));  // open: en
endmodule

module button1 (
  output [3:0] out_1,
  output [3:0] out_2,
  output out_3,
  output out_4,
  output out_5,
  output out_6,
  output out_7,
  output out_8,
  output out_9,
  output out_10
);

  wire B7, B8, B9, B12, B13, B14, B17, B17_out, B18, B19, CLK, D7, D8, D9, D12, D13, D14, D17, D18, D19,
       d_ff_1_q, d_ff_2_q, demultiplexer_1_out0, demultiplexer_1_out1, demultiplexer_1_out2,
       demultiplexer_1_out3, demultiplexer_1_out8, demultiplexer_1_out9, demultiplexer_1_out10,
       demultiplexer_1_out11, demultiplexer_1_out12, demultiplexer_1_out13, demultiplexer_1_out14,
       demultiplexer_1_out15, en, G17, not_1_out, or_1_out, or_2_out, or_3_out, or_4_out, or_5_out, or_6_out,
       or_7_out, or_8_out, or_9_out, R7, R8, R9, R12, R13, R14, R17, R18, R19, register_1_q, register_2_q,
       register_3_q, register_4_q, register_5_q, register_6_q, register_7_q, register_8_q, register_9_q, rst,
       xor_1_out, xor_2_out, xor_3_out, xor_4_out, xor_5_out, xor_6_out, xor_7_out, xor_8_out, xor_9_out;

  and and_1 (B17, B17_out, G17);
  Button u_B18 (.out(B18));
  Button u_B17 (.out(B17_out));
  Button u_B13 (.out(B13));
  Button u_B12 (.out(B12));
  Button u_B8 (.out(B8));
  Button u_B7 (.out(B7));
  Button u_B19 (.out(B19));
  Button u_B14 (.out(B14));
  Button u_rst (.out(rst));
  Button u_B9 (.out(B9));
  or or_1 (or_1_out, B12, B17, B18);
  or or_2 (or_2_out, B7, B12, B17, B13);
  or or_3 (or_3_out, B12, B7, B8);
  Clock clock_1 (.out(CLK));
  state state_1 (.out(G17), .B(or_1_out), .rst(rst), .R(R17), .clk(CLK));
  state state_2 (.out(out_5), .B(or_2_out), .rst(rst), .R(R12), .clk(CLK));
  state state_3 (.out(out_8), .B(or_3_out), .rst(rst), .R(R7), .clk(CLK));
  or or_4 (or_4_out, B19, B17, B18, B13);
  or or_5 (or_5_out, B18, B12, B13, B14, B8);
  or or_6 (or_6_out, B13, B8, B9, B7);
  state state_4 (.out(out_3), .B(or_4_out), .rst(rst), .R(R18), .clk(CLK));
  state state_5 (.out(out_6), .B(or_5_out), .rst(rst), .R(R13), .clk(CLK));
  state state_6 (.out(out_9), .B(or_6_out), .rst(rst), .R(R8), .clk(CLK));
  or or_7 (or_7_out, B14, B19, B18);
  or or_8 (or_8_out, B13, B19, B14, B9);
  or or_9 (or_9_out, B9, B14, B8);
  state state_7 (.out(out_4), .B(or_7_out), .rst(rst), .R(R19), .clk(CLK));
  state state_8 (.out(out_7), .B(or_8_out), .rst(rst), .R(R14), .clk(CLK));
  state state_9 (.out(out_10), .B(or_9_out), .rst(rst), .R(R9), .clk(CLK));
  or or_10 (D13, demultiplexer_1_out0, demultiplexer_1_out1, demultiplexer_1_out2, demultiplexer_1_out3);
  Random #(.width(4), .trigger("falling")) random_1 (.clk(CLK), .next(1'b1), .out(out_1));  // open: clr
  Demultiplexer #(.select(4)) demultiplexer_1 (
    .out0(demultiplexer_1_out0), .out1(demultiplexer_1_out1), .out2(demultiplexer_1_out2),
    .out3(demultiplexer_1_out3), .out4(D7), .out5(D19), .out6(D9), .out7(D17), .out8(demultiplexer_1_out8),
    .out9(demultiplexer_1_out9), .out10(demultiplexer_1_out10), .out11(demultiplexer_1_out11),
    .out12(demultiplexer_1_out12), .out13(demultiplexer_1_out13), .out14(demultiplexer_1_out14),
    .out15(demultiplexer_1_out15), .in(1'b1), .sel(out_2), .en(rst));
  or or_11 (D18, demultiplexer_1_out10, demultiplexer_1_out11);
  or or_12 (D8, demultiplexer_1_out8, demultiplexer_1_out9);
  Register #(.width(4)) rst_2 (.D(out_1), .Q(out_2), .clk(rst));  // open: en, clr
  or or_13 (D14, demultiplexer_1_out14, demultiplexer_1_out15);
  or or_14 (D12, demultiplexer_1_out12, demultiplexer_1_out13);
  Register #(.width(1), .trigger("high")) register_1 (.D(D7), .Q(register_1_q), .clk(en));  // open: en, clr
  Register #(.width(1), .trigger("high")) register_2 (.D(D8), .Q(register_2_q), .clk(en));  // open: en, clr
  Register #(.width(1), .trigger("high")) register_3 (.D(D9), .Q(register_3_q), .clk(en));  // open: en, clr
  Register #(.width(1), .trigger("high")) register_4 (.D(D12), .Q(register_4_q), .clk(en));  // open: en, clr
  Register #(.width(1), .trigger("high")) register_5 (.D(D13), .Q(register_5_q), .clk(en));  // open: en, clr
  Register #(.width(1), .trigger("high")) register_6 (.D(D14), .Q(register_6_q), .clk(en));  // open: en, clr
  Register #(.width(1), .trigger("high")) register_7 (.D(D17), .Q(register_7_q), .clk(en));  // open: en, clr
  Register #(.width(1), .trigger("high")) register_8 (.D(D18), .Q(register_8_q), .clk(en));  // open: en, clr
  Register #(.width(1), .trigger("high")) register_9 (.D(D19), .Q(register_9_q), .clk(en));  // open: en, clr
  D_Flip_Flop d_ff_1 (.clk(CLK), .D(rst), .Q(d_ff_1_q));  // open: Qn, preset, en, reset
  xor xor_1 (xor_1_out, rst, register_1_q);
  xor xor_2 (xor_2_out, rst, register_2_q);
  xor xor_3 (xor_3_out, rst, register_3_q);
  xor xor_4 (xor_4_out, rst, register_4_q);
  xor xor_5 (xor_5_out, rst, register_5_q);
  xor xor_6 (xor_6_out, rst, register_6_q);
  xor xor_7 (xor_7_out, rst, register_7_q);
  xor xor_8 (xor_8_out, rst, register_8_q);
  xor xor_9 (xor_9_out, rst, register_9_q);
  not not_1 (not_1_out, d_ff_2_q);
  D_Flip_Flop d_ff_2 (.clk(CLK), .D(d_ff_1_q), .Q(d_ff_2_q));  // open: Qn, preset, en, reset
  and and_2 (R7, rst, xor_1_out);
  and and_3 (R8, rst, xor_2_out);
  and and_4 (R9, rst, xor_3_out);
  and and_5 (R12, rst, xor_4_out);
  and and_6 (R13, rst, xor_5_out);
  and and_7 (R14, rst, xor_6_out);
  and and_8 (R17, rst, xor_7_out);
  and and_9 (R18, rst, xor_8_out);
  and and_10 (R19, rst, xor_9_out);
  and and_11 (en, not_1_out, d_ff_1_q);

  // Other names for the same wires on the sheet: SELECT[3:0] = out_2
endmodule

module state (
  input  clk,
  input  rst,
  input  R,
  input  B,
  output out
);

  wire adder_1_out, and_1_out, d_ff_1_q, or_1_out, register_1_q, xor_1_out;

  Adder #(.width(1)) adder_1 (.a(out), .b(1'b0), .out(adder_1_out), .cin(1'b1));  // open: cout
  Register #(.width(1)) register_1 (.D(adder_1_out), .Q(register_1_q), .clk(or_1_out), .clr(R));  // open: en
  or or_1 (or_1_out, B, rst);
  xor xor_1 (xor_1_out, rst, R);
  and and_1 (and_1_out, or_1_out, clk);
  Multiplexer multiplexer_1 (.in0(register_1_q), .in1(d_ff_1_q), .out(out), .sel(d_ff_1_q));  // open: en
  D_Flip_Flop d_ff_1 (.clk(and_1_out), .D(xor_1_out), .Q(d_ff_1_q));  // open: Qn, preset, en, reset
endmodule

module state1 (
  input  B,
  input  rst,
  input  R,
  output out,
  output out_2,
  output out_3
);

  wire adder_1_out, adder_2_out, and_1_out, button_1_out, button_2_out, button_3_out, button_4_out,
       button_5_out, clock_1_out, clock_2_out, counter_1_carry, d_ff_1_qn, d_ff_2_q, d_ff_3_q, d_ff_4_q,
       multiplexer_1_out, multiplexer_3_out, not_1_out, or_1_out, or_2_out, or_3_out, or_4_out, register_1_q,
       register_2_q, xor_1_out;

  Button button_1 (.out(button_1_out));
  Register #(.width(1)) register_1 (.D(out_3), .Q(register_1_q), .clk(or_1_out), .clr(R));  // open: en
  or or_1 (or_1_out, B, rst);
  Clock #(.lowDuration(10)) clock_1 (.out(clock_1_out));
  Adder #(.width(1)) adder_1 (.a(register_1_q), .b(1'b0), .out(adder_1_out), .cin(1'b1));  // open: cout
  Multiplexer multiplexer_1 (.in0(1'b0), .in1(1'b1), .out(multiplexer_1_out), .sel(counter_1_carry));  // open: en
  or or_2 (or_2_out, button_1_out, multiplexer_1_out);
  Counter #(.width(1), .max('h1)) counter_1 (
    .D(out), .count(d_ff_1_qn), .Q(out), .carry(counter_1_carry), .clk(clock_1_out), .clr(or_3_out));  // open: load
  D_Flip_Flop d_ff_1 (.clk(or_2_out), .D(multiplexer_1_out), .Qn(d_ff_1_qn));  // open: Q, preset, en, reset
  or or_3 (or_3_out, button_1_out, counter_1_carry);
  xor xor_1 (xor_1_out, rst, R);
  Multiplexer multiplexer_2 (.in0(adder_1_out), .in1(xor_1_out), .out(out_3), .sel(d_ff_2_q));  // open: en
  D_Flip_Flop d_ff_2 (.D(rst), .Q(d_ff_2_q));  // open: clk, Qn, preset, en, reset
  Button button_2 (.out(button_2_out));
  D_Flip_Flop d_ff_3 (.clk(button_2_out), .D(1'b1), .Q(d_ff_3_q));  // open: Qn, preset, en, reset
  Adder #(.width(1)) adder_2 (.a(out_2), .b(1'b0), .out(adder_2_out), .cin(1'b1));  // open: cout
  Button button_3 (.out(button_3_out));
  or or_4 (or_4_out, button_3_out, button_5_out);
  D_Flip_Flop d_ff_4 (.clk(button_2_out), .D(d_ff_3_q), .Q(d_ff_4_q));  // open: Qn, preset, en, reset
  not not_1 (not_1_out, d_ff_4_q);
  Register #(.width(1)) register_2 (.D(adder_2_out), .Q(register_2_q), .clk(or_4_out), .clr(button_4_out));  // open: en
  Button button_4 (.out(button_4_out));
  and and_1 (and_1_out, not_1_out, d_ff_3_q);
  Multiplexer multiplexer_3 (.in0(register_2_q), .in1(1'b1), .out(multiplexer_3_out), .sel(button_5_out));  // open: en
  Button button_5 (.out(button_5_out));
  D_Flip_Flop d_ff_5 ();  // open: clk, D, Q, Qn, preset, en, reset
  Register #(.width(1)) register_3 (.D(multiplexer_3_out), .Q(out_2), .clk(clock_2_out));  // open: en, clr
  Clock #(.lowDuration(10)) clock_2 (.out(clock_2_out));
endmodule

module state2 (
  input  in_1,
  input  in_2,
  input  in_3,
  input  in_4,
  output out
);

  wire adder_1_out, multiplexer_1_out, or_1_out, register_1_q;

  Adder #(.width(1)) adder_1 (.a(out), .b(1'b0), .out(adder_1_out), .cin(1'b1));  // open: cout
  Button button_1 (.out(in_3));
  Register #(.width(1)) register_1 (.D(adder_1_out), .Q(register_1_q), .clk(or_1_out), .clr(in_1));  // open: en
  Button button_2 (.out(in_1));
  or or_1 (or_1_out, in_3, in_4);
  Button button_3 (.out(in_4));
  Multiplexer multiplexer_1 (.in0(register_1_q), .in1(1'b1), .out(multiplexer_1_out), .sel(in_4));  // open: en
  Register #(.width(1)) register_2 (.D(multiplexer_1_out), .Q(out), .clk(in_2));  // open: en, clr
endmodule

// bottom
module Fire (
  input  B,
  output [4:0] out_2,
  output [4:0] out_3,
  output [4:0] out_4,
  output [4:0] out_5,
  output [4:0] out_6
);

  wire clock_1_out, counter_1_carry, counter_2_carry, counter_3_carry, counter_4_carry, counter_5_carry,
       d_ff_1_qn, d_ff_2_qn, d_ff_3_qn, d_ff_4_qn, d_ff_5_qn, multiplexer_1_out, multiplexer_2_out,
       multiplexer_3_out, multiplexer_4_out, multiplexer_5_out, or_1_out, or_2_out, or_3_out, or_4_out,
       or_5_out, or_6_out, or_7_out, or_8_out, or_9_out, or_10_out;
  wire [2:0] counter_1_q, counter_2_q, counter_3_q, counter_4_q, counter_5_q;
  wire [3:0] multiplexer_6_out, multiplexer_7_out, multiplexer_8_out, multiplexer_9_out, multiplexer_10_out,
       random_1_out, random_2_out, random_3_out, random_4_out, random_5_out;

  Clock #(.lowDuration(10)) clock_1 (.out(clock_1_out));
  Multiplexer multiplexer_1 (.in0(1'b0), .in1(1'b1), .out(multiplexer_1_out), .sel(counter_1_carry));  // open: en
  Multiplexer multiplexer_2 (.in0(1'b0), .in1(1'b1), .out(multiplexer_2_out), .sel(counter_2_carry));  // open: en
  Multiplexer multiplexer_3 (.in0(1'b0), .in1(1'b1), .out(multiplexer_3_out), .sel(counter_3_carry));  // open: en
  Multiplexer multiplexer_4 (.in0(1'b0), .in1(1'b1), .out(multiplexer_4_out), .sel(counter_4_carry));  // open: en
  Multiplexer multiplexer_5 (.in0(1'b0), .in1(1'b1), .out(multiplexer_5_out), .sel(counter_5_carry));  // open: en
  or or_1 (or_1_out, B, multiplexer_1_out);
  or or_2 (or_2_out, B, multiplexer_2_out);
  or or_3 (or_3_out, B, multiplexer_3_out);
  or or_4 (or_4_out, B, multiplexer_4_out);
  or or_5 (or_5_out, B, multiplexer_5_out);
  D_Flip_Flop d_ff_1 (.clk(or_1_out), .D(multiplexer_1_out), .Qn(d_ff_1_qn));  // open: Q, preset, en, reset
  D_Flip_Flop d_ff_2 (.clk(or_2_out), .D(multiplexer_2_out), .Qn(d_ff_2_qn));  // open: Q, preset, en, reset
  D_Flip_Flop d_ff_3 (.clk(or_3_out), .D(multiplexer_3_out), .Qn(d_ff_3_qn));  // open: Q, preset, en, reset
  D_Flip_Flop d_ff_4 (.clk(or_4_out), .D(multiplexer_4_out), .Qn(d_ff_4_qn));  // open: Q, preset, en, reset
  D_Flip_Flop d_ff_5 (.clk(or_5_out), .D(multiplexer_5_out), .Qn(d_ff_5_qn));  // open: Q, preset, en, reset
  Counter #(.width(3), .max('h7)) counter_1 (
    .D(counter_1_q), .count(d_ff_1_qn), .Q(counter_1_q), .carry(counter_1_carry), .clk(clock_1_out),
    .clr(or_6_out));  // open: load
  or or_6 (or_6_out, B, counter_1_carry);
  Counter #(.width(3), .max('h7)) counter_2 (
    .D(counter_2_q), .count(d_ff_2_qn), .Q(counter_2_q), .carry(counter_2_carry), .clk(clock_1_out),
    .clr(or_7_out));  // open: load
  or or_7 (or_7_out, B, counter_2_carry);
  Counter #(.width(3), .max('h7)) counter_3 (
    .D(counter_3_q), .count(d_ff_3_qn), .Q(counter_3_q), .carry(counter_3_carry), .clk(clock_1_out),
    .clr(or_8_out));  // open: load
  or or_8 (or_8_out, B, counter_3_carry);
  Counter #(.width(3), .max('h7)) counter_4 (
    .D(counter_4_q), .count(d_ff_4_qn), .Q(counter_4_q), .carry(counter_4_carry), .clk(clock_1_out),
    .clr(or_9_out));  // open: load
  or or_9 (or_9_out, B, counter_4_carry);
  Counter #(.width(3), .max('h7)) counter_5 (
    .D(counter_5_q), .count(d_ff_5_qn), .Q(counter_5_q), .carry(counter_5_carry), .clk(clock_1_out),
    .clr(or_10_out));  // open: load
  or or_10 (or_10_out, B, counter_5_carry);
  Random #(.width(4), .trigger("falling")) random_1 (
    .clk(clock_1_out), .next(d_ff_1_qn), .out(random_1_out));  // open: clr
  Random #(.width(4), .trigger("falling")) random_2 (
    .clk(clock_1_out), .next(d_ff_2_qn), .out(random_2_out));  // open: clr
  Random #(.width(4), .trigger("falling")) random_3 (
    .clk(clock_1_out), .next(d_ff_3_qn), .out(random_3_out));  // open: clr
  Random #(.width(4), .trigger("falling")) random_4 (
    .clk(clock_1_out), .next(d_ff_4_qn), .out(random_4_out));  // open: clr
  Random #(.width(4), .trigger("falling")) random_5 (
    .clk(clock_1_out), .next(d_ff_5_qn), .out(random_5_out));  // open: clr
  Bit_Extender #(.in_width(4), .out_width(5), .\type ("input")) bit_extender_1 (
    .in(multiplexer_6_out), .out(out_2));  // open: extend
  Multiplexer #(.width(4)) multiplexer_6 (
    .in0(4'b0000), .in1(random_1_out), .out(multiplexer_6_out), .sel(d_ff_1_qn));  // open: en
  Multiplexer #(.width(4)) multiplexer_7 (
    .in0(4'b0000), .in1(random_2_out), .out(multiplexer_7_out), .sel(d_ff_2_qn));  // open: en
  Bit_Extender #(.in_width(4), .out_width(5), .\type ("input")) bit_extender_2 (
    .in(multiplexer_7_out), .out(out_3));  // open: extend
  Multiplexer #(.width(4)) multiplexer_8 (
    .in0(4'b0000), .in1(random_3_out), .out(multiplexer_8_out), .sel(d_ff_3_qn));  // open: en
  Bit_Extender #(.in_width(4), .out_width(5), .\type ("input")) bit_extender_3 (
    .in(multiplexer_8_out), .out(out_4));  // open: extend
  Bit_Extender #(.in_width(4), .out_width(5), .\type ("input")) bit_extender_4 (
    .in(multiplexer_9_out), .out(out_5));  // open: extend
  Multiplexer #(.width(4)) multiplexer_9 (
    .in0(4'b0000), .in1(random_4_out), .out(multiplexer_9_out), .sel(d_ff_4_qn));  // open: en
  Bit_Extender #(.in_width(4), .out_width(5), .\type ("input")) bit_extender_5 (
    .in(multiplexer_10_out), .out(out_6));  // open: extend
  Multiplexer #(.width(4)) multiplexer_10 (
    .in0(4'b0000), .in1(random_5_out), .out(multiplexer_10_out), .sel(d_ff_5_qn));  // open: en
endmodule

// top
module Fire_top (
  input  B,
  output [4:0] out_2,
  output [4:0] out_3,
  output [4:0] out_4,
  output [4:0] out_5,
  output [4:0] out_6
);

  wire clock_1_out, counter_1_carry, counter_2_carry, counter_3_carry, counter_4_carry, counter_5_carry,
       d_ff_1_qn, d_ff_2_qn, d_ff_3_qn, d_ff_4_qn, d_ff_5_qn, multiplexer_1_out, multiplexer_2_out,
       multiplexer_3_out, multiplexer_4_out, multiplexer_5_out, or_1_out, or_2_out, or_3_out, or_4_out,
       or_5_out, or_6_out, or_7_out, or_8_out, or_9_out, or_10_out;
  wire [2:0] counter_1_q, counter_2_q, counter_3_q, counter_4_q, counter_5_q;
  wire [3:0] random_1_out, random_2_out, random_3_out, random_4_out, random_5_out;

  Clock #(.lowDuration(10)) clock_1 (.out(clock_1_out));
  Multiplexer multiplexer_1 (.in0(1'b0), .in1(1'b1), .out(multiplexer_1_out), .sel(counter_1_carry));  // open: en
  Multiplexer multiplexer_2 (.in0(1'b0), .in1(1'b1), .out(multiplexer_2_out), .sel(counter_2_carry));  // open: en
  Multiplexer multiplexer_3 (.in0(1'b0), .in1(1'b1), .out(multiplexer_3_out), .sel(counter_3_carry));  // open: en
  Multiplexer multiplexer_4 (.in0(1'b0), .in1(1'b1), .out(multiplexer_4_out), .sel(counter_4_carry));  // open: en
  Multiplexer multiplexer_5 (.in0(1'b0), .in1(1'b1), .out(multiplexer_5_out), .sel(counter_5_carry));  // open: en
  or or_1 (or_1_out, B, multiplexer_1_out);
  or or_2 (or_2_out, B, multiplexer_2_out);
  or or_3 (or_3_out, B, multiplexer_3_out);
  or or_4 (or_4_out, B, multiplexer_4_out);
  or or_5 (or_5_out, B, multiplexer_5_out);
  D_Flip_Flop d_ff_1 (.clk(or_1_out), .D(multiplexer_1_out), .Qn(d_ff_1_qn));  // open: Q, preset, en, reset
  D_Flip_Flop d_ff_2 (.clk(or_2_out), .D(multiplexer_2_out), .Qn(d_ff_2_qn));  // open: Q, preset, en, reset
  D_Flip_Flop d_ff_3 (.clk(or_3_out), .D(multiplexer_3_out), .Qn(d_ff_3_qn));  // open: Q, preset, en, reset
  D_Flip_Flop d_ff_4 (.clk(or_4_out), .D(multiplexer_4_out), .Qn(d_ff_4_qn));  // open: Q, preset, en, reset
  D_Flip_Flop d_ff_5 (.clk(or_5_out), .D(multiplexer_5_out), .Qn(d_ff_5_qn));  // open: Q, preset, en, reset
  Counter #(.width(3), .max('h7)) counter_1 (
    .D(counter_1_q), .count(d_ff_1_qn), .Q(counter_1_q), .carry(counter_1_carry), .clk(clock_1_out),
    .clr(or_6_out));  // open: load
  or or_6 (or_6_out, B, counter_1_carry);
  Counter #(.width(3), .max('h7)) counter_2 (
    .D(counter_2_q), .count(d_ff_2_qn), .Q(counter_2_q), .carry(counter_2_carry), .clk(clock_1_out),
    .clr(or_7_out));  // open: load
  or or_7 (or_7_out, B, counter_2_carry);
  Counter #(.width(3), .max('h7)) counter_3 (
    .D(counter_3_q), .count(d_ff_3_qn), .Q(counter_3_q), .carry(counter_3_carry), .clk(clock_1_out),
    .clr(or_8_out));  // open: load
  or or_8 (or_8_out, B, counter_3_carry);
  Counter #(.width(3), .max('h7)) counter_4 (
    .D(counter_4_q), .count(d_ff_4_qn), .Q(counter_4_q), .carry(counter_4_carry), .clk(clock_1_out),
    .clr(or_9_out));  // open: load
  or or_9 (or_9_out, B, counter_4_carry);
  Counter #(.width(3), .max('h7)) counter_5 (
    .D(counter_5_q), .count(d_ff_5_qn), .Q(counter_5_q), .carry(counter_5_carry), .clk(clock_1_out),
    .clr(or_10_out));  // open: load
  or or_10 (or_10_out, B, counter_5_carry);
  Random #(.width(4), .trigger("falling")) random_1 (
    .clk(clock_1_out), .next(d_ff_1_qn), .out(random_1_out));  // open: clr
  Random #(.width(4), .trigger("falling")) random_2 (
    .clk(clock_1_out), .next(d_ff_2_qn), .out(random_2_out));  // open: clr
  Random #(.width(4), .trigger("falling")) random_3 (
    .clk(clock_1_out), .next(d_ff_3_qn), .out(random_3_out));  // open: clr
  Random #(.width(4), .trigger("falling")) random_4 (
    .clk(clock_1_out), .next(d_ff_4_qn), .out(random_4_out));  // open: clr
  Random #(.width(4), .trigger("falling")) random_5 (
    .clk(clock_1_out), .next(d_ff_5_qn), .out(random_5_out));  // open: clr
  Multiplexer #(.width(4)) multiplexer_6 (
    .in0(4'b0000), .in1(random_1_out), .out(out_2[4:1]), .sel(d_ff_1_qn));  // open: en
  Multiplexer #(.width(4)) multiplexer_7 (
    .in0(4'b0000), .in1(random_2_out), .out(out_3[4:1]), .sel(d_ff_2_qn));  // open: en
  Multiplexer #(.width(4)) multiplexer_8 (
    .in0(4'b0000), .in1(random_3_out), .out(out_4[4:1]), .sel(d_ff_3_qn));  // open: en
  Multiplexer #(.width(4)) multiplexer_9 (
    .in0(4'b0000), .in1(random_4_out), .out(out_5[4:1]), .sel(d_ff_4_qn));  // open: en
  Multiplexer #(.width(4)) multiplexer_10 (
    .in0(4'b0000), .in1(random_5_out), .out(out_6[4:1]), .sel(d_ff_5_qn));  // open: en
endmodule

module right (
  input  B1,
  input  B2,
  input  B3,
  output [14:0] out_4,
  output [14:0] out_5,
  output [14:0] out_6,
  output [14:0] out_7
);

  wire clock_1_out, counter_1_carry, counter_2_carry, counter_3_carry, d_ff_1_qn, d_ff_2_qn, d_ff_3_qn,
       demultiplexer_1_out0, demultiplexer_1_out1, demultiplexer_1_out2, demultiplexer_1_out3,
       demultiplexer_1_out4, demultiplexer_1_out5, demultiplexer_1_out6, demultiplexer_1_out7,
       demultiplexer_2_out0, demultiplexer_2_out1, demultiplexer_2_out2, demultiplexer_2_out3,
       demultiplexer_2_out4, demultiplexer_2_out5, demultiplexer_2_out6, demultiplexer_2_out7,
       demultiplexer_3_out0, demultiplexer_3_out1, demultiplexer_3_out2, demultiplexer_3_out3,
       demultiplexer_3_out4, demultiplexer_3_out5, demultiplexer_3_out6, demultiplexer_3_out7,
       multiplexer_1_out, multiplexer_2_out, multiplexer_3_out, or_1_out, or_2_out, or_3_out, or_4_out,
       or_5_out, or_6_out, or_7_out, or_8_out, or_9_out, or_10_out, or_11_out, or_12_out, or_13_out,
       or_14_out, or_15_out, or_16_out, or_17_out, or_18_out;
  wire [2:0] counter_1_q, counter_2_q, counter_3_q;
  wire [4:0] rom_1_data, rom_2_data, rom_3_data;

  Clock #(.lowDuration(10)) clock_1 (.out(clock_1_out));
  Multiplexer multiplexer_1 (.in0(1'b0), .in1(1'b1), .out(multiplexer_1_out), .sel(counter_1_carry));  // open: en
  Multiplexer multiplexer_2 (.in0(1'b0), .in1(1'b1), .out(multiplexer_2_out), .sel(counter_2_carry));  // open: en
  Multiplexer multiplexer_3 (.in0(1'b0), .in1(1'b1), .out(multiplexer_3_out), .sel(counter_3_carry));  // open: en
  or or_1 (or_1_out, B1, multiplexer_1_out);
  or or_2 (or_2_out, B2, multiplexer_2_out);
  or or_3 (or_3_out, B3, multiplexer_3_out);
  D_Flip_Flop d_ff_1 (.clk(or_1_out), .D(multiplexer_1_out), .Qn(d_ff_1_qn));  // open: Q, preset, en, reset
  D_Flip_Flop d_ff_2 (.clk(or_2_out), .D(multiplexer_2_out), .Qn(d_ff_2_qn));  // open: Q, preset, en, reset
  D_Flip_Flop d_ff_3 (.clk(or_3_out), .D(multiplexer_3_out), .Qn(d_ff_3_qn));  // open: Q, preset, en, reset
  Counter #(.width(3), .max('h7)) counter_1 (
    .D(counter_1_q), .count(d_ff_1_qn), .Q(counter_1_q), .carry(counter_1_carry), .clk(clock_1_out),
    .clr(or_4_out));  // open: load
  or or_4 (or_4_out, B1, counter_1_carry);
  Counter #(.width(3), .max('h7)) counter_2 (
    .D(counter_2_q), .count(d_ff_2_qn), .Q(counter_2_q), .carry(counter_2_carry), .clk(clock_1_out),
    .clr(or_5_out));  // open: load
  or or_5 (or_5_out, B2, counter_2_carry);
  Counter #(.width(3), .max('h7)) counter_3 (
    .D(counter_3_q), .count(d_ff_3_qn), .Q(counter_3_q), .carry(counter_3_carry), .clk(clock_1_out),
    .clr(or_6_out));  // open: load
  or or_6 (or_6_out, B3, counter_3_carry);
  ROM #(.addrWidth(3), .dataWidth(5)) rom_1 (.addr(counter_1_q), .data(rom_1_data));  // open: sel
  ROM #(.addrWidth(3), .dataWidth(5)) rom_2 (.addr(counter_2_q), .data(rom_2_data));  // open: sel
  ROM #(.addrWidth(3), .dataWidth(5)) rom_3 (.addr(counter_3_q), .data(rom_3_data));  // open: sel
  Demultiplexer #(.select(3)) demultiplexer_1 (
    .out0(demultiplexer_1_out0), .out1(demultiplexer_1_out1), .out2(demultiplexer_1_out2),
    .out3(demultiplexer_1_out3), .out4(demultiplexer_1_out4), .out5(demultiplexer_1_out5),
    .out6(demultiplexer_1_out6), .out7(demultiplexer_1_out7), .in(1'b1), .sel(counter_1_q));  // open: en
  Demultiplexer #(.select(3)) demultiplexer_2 (
    .out0(demultiplexer_2_out0), .out1(demultiplexer_2_out1), .out2(demultiplexer_2_out2),
    .out3(demultiplexer_2_out3), .out4(demultiplexer_2_out4), .out5(demultiplexer_2_out5),
    .out6(demultiplexer_2_out6), .out7(demultiplexer_2_out7), .in(1'b1), .sel(counter_2_q));  // open: en
  Demultiplexer #(.select(3)) demultiplexer_3 (
    .out0(demultiplexer_3_out0), .out1(demultiplexer_3_out1), .out2(demultiplexer_3_out2),
    .out3(demultiplexer_3_out3), .out4(demultiplexer_3_out4), .out5(demultiplexer_3_out5),
    .out6(demultiplexer_3_out6), .out7(demultiplexer_3_out7), .in(1'b1), .sel(counter_3_q));  // open: en
  or or_7 (or_7_out, demultiplexer_1_out3, demultiplexer_1_out4);
  or or_8 (or_8_out, demultiplexer_2_out3, demultiplexer_2_out4);
  or or_9 (or_9_out, demultiplexer_3_out3, demultiplexer_3_out4);
  Multiplexer #(.width(5)) multiplexer_4 (
    .in0({5{1'b0}}), .in1(rom_1_data), .out(out_4[4:0]), .sel(or_7_out));  // open: en
  or or_10 (or_10_out, demultiplexer_1_out2, demultiplexer_1_out5);
  Multiplexer #(.width(5)) multiplexer_5 (
    .in0({5{1'b0}}), .in1(rom_2_data), .out(out_4[9:5]), .sel(or_8_out));  // open: en
  or or_11 (or_11_out, demultiplexer_2_out2, demultiplexer_2_out5);
  Multiplexer #(.width(5)) multiplexer_6 (
    .in0({5{1'b0}}), .in1(rom_3_data), .out(out_4[14:10]), .sel(or_9_out));  // open: en
  or or_12 (or_12_out, demultiplexer_3_out2, demultiplexer_3_out5);
  Multiplexer #(.width(5)) multiplexer_7 (
    .in0({5{1'b0}}), .in1(rom_1_data), .out(out_5[4:0]), .sel(or_10_out));  // open: en
  Multiplexer #(.width(5)) multiplexer_8 (
    .in0({5{1'b0}}), .in1(rom_1_data), .out(out_6[4:0]), .sel(or_13_out));  // open: en
  or or_13 (or_13_out, demultiplexer_1_out1, demultiplexer_1_out6);
  Multiplexer #(.width(5)) multiplexer_9 (
    .in0({5{1'b0}}), .in1(rom_2_data), .out(out_6[9:5]), .sel(or_14_out));  // open: en
  Multiplexer #(.width(5)) multiplexer_10 (
    .in0({5{1'b0}}), .in1(rom_2_data), .out(out_5[9:5]), .sel(or_11_out));  // open: en
  or or_14 (or_14_out, demultiplexer_2_out1, demultiplexer_2_out6);
  Multiplexer #(.width(5)) multiplexer_11 (
    .in0({5{1'b0}}), .in1(rom_3_data), .out(out_5[14:10]), .sel(or_12_out));  // open: en
  Multiplexer #(.width(5)) multiplexer_12 (
    .in0({5{1'b0}}), .in1(rom_3_data), .out(out_6[14:10]), .sel(or_15_out));  // open: en
  or or_15 (or_15_out, demultiplexer_3_out1, demultiplexer_3_out6);
  Multiplexer #(.width(5)) multiplexer_13 (
    .in0({5{1'b0}}), .in1(rom_1_data), .out(out_7[4:0]), .sel(or_16_out));  // open: en
  or or_16 (or_16_out, demultiplexer_1_out0, demultiplexer_1_out7);
  Multiplexer #(.width(5)) multiplexer_14 (
    .in0({5{1'b0}}), .in1(rom_2_data), .out(out_7[9:5]), .sel(or_17_out));  // open: en
  or or_17 (or_17_out, demultiplexer_2_out0, demultiplexer_2_out7);
  Multiplexer #(.width(5)) multiplexer_15 (
    .in0({5{1'b0}}), .in1(rom_3_data), .out(out_7[14:10]), .sel(or_18_out));  // open: en
  or or_18 (or_18_out, demultiplexer_3_out0, demultiplexer_3_out7);

  // Notes on the sheet:
  //   contents of rom_1 (hex, n*v repeats v):
  //   0 4 a 11 a 4 4
  //   contents of rom_2 (hex, n*v repeats v):
  //   0 4 a 11 a 4 4
  //   contents of rom_3 (hex, n*v repeats v):
  //   0 4 a 11 a 4 4
endmodule

module GG (
  input  GG,
  output [10:0] out_2,
  output [10:0] out_3,
  output [10:0] out_4,
  output [10:0] out_5,
  output [10:0] out_6,
  output [10:0] out_7,
  output [10:0] out_8,
  output [10:0] out_9,
  output [10:0] out_10,
  output [10:0] out_11,
  output [10:0] out_12
);

  wire and_1_out, clock_1_out, clock_2_out, counter_1_carry, d_ff_1_q, d_ff_2_q, d_ff_3_qn,
       multiplexer_1_out, not_1_out, or_1_out, or_2_out;
  wire [3:0] counter_1_q;
  wire [10:0] rom_1_data, rom_2_data, rom_3_data, rom_4_data, rom_5_data, rom_6_data, rom_7_data, rom_8_data,
       rom_9_data, rom_10_data, rom_11_data;

  Clock clock_1 (.out(clock_1_out));
  D_Flip_Flop d_ff_1 (.clk(clock_1_out), .D(GG), .Q(d_ff_1_q));  // open: Qn, preset, en, reset
  D_Flip_Flop d_ff_2 (.clk(clock_1_out), .D(d_ff_1_q), .Q(d_ff_2_q));  // open: Qn, preset, en, reset
  not not_1 (not_1_out, d_ff_2_q);
  Clock #(.lowDuration(20)) clock_2 (.out(clock_2_out));
  and and_1 (and_1_out, not_1_out, d_ff_1_q);
  Multiplexer multiplexer_1 (.in0(1'b0), .in1(1'b1), .out(multiplexer_1_out), .sel(counter_1_carry));  // open: en
  or or_1 (or_1_out, and_1_out, multiplexer_1_out);
  D_Flip_Flop d_ff_3 (.clk(or_1_out), .D(multiplexer_1_out), .Qn(d_ff_3_qn));  // open: Q, preset, en, reset
  Counter #(.width(4), .max('hf)) counter_1 (
    .D(counter_1_q), .count(d_ff_3_qn), .Q(counter_1_q), .carry(counter_1_carry), .clk(clock_2_out),
    .clr(or_2_out));  // open: load
  or or_2 (or_2_out, and_1_out, counter_1_carry);
  Multiplexer #(.width(11)) multiplexer_2 (.in0(rom_1_data), .out(out_7), .sel(1'b0));  // open: in1, en
  ROM #(.addrWidth(4), .dataWidth(11)) rom_1 (.addr(counter_1_q), .data(rom_1_data));  // open: sel
  ROM #(.addrWidth(4), .dataWidth(11)) rom_2 (.addr(counter_1_q), .data(rom_2_data));  // open: sel
  Multiplexer #(.width(11)) multiplexer_3 (.in0(rom_3_data), .out(out_8), .sel(1'b0));  // open: in1, en
  Multiplexer #(.width(11)) multiplexer_4 (.in0(rom_2_data), .out(out_2), .sel(1'b0));  // open: in1, en
  ROM #(.addrWidth(4), .dataWidth(11)) rom_3 (.addr(counter_1_q), .data(rom_3_data));  // open: sel
  ROM #(.addrWidth(4), .dataWidth(11)) rom_4 (.addr(counter_1_q), .data(rom_4_data));  // open: sel
  Multiplexer #(.width(11)) multiplexer_5 (.in0(rom_5_data), .out(out_9), .sel(1'b0));  // open: in1, en
  Multiplexer #(.width(11)) multiplexer_6 (.in0(rom_4_data), .out(out_3), .sel(1'b0));  // open: in1, en
  ROM #(.addrWidth(4), .dataWidth(11)) rom_5 (.addr(counter_1_q), .data(rom_5_data));  // open: sel
  Multiplexer #(.width(11)) multiplexer_7 (.in0(rom_6_data), .out(out_4), .sel(1'b0));  // open: in1, en
  ROM #(.addrWidth(4), .dataWidth(11)) rom_6 (.addr(counter_1_q), .data(rom_6_data));  // open: sel
  ROM #(.addrWidth(4), .dataWidth(11)) rom_7 (.addr(counter_1_q), .data(rom_7_data));  // open: sel
  Multiplexer #(.width(11)) multiplexer_8 (.in0(rom_8_data), .out(out_5), .sel(1'b0));  // open: in1, en
  Multiplexer #(.width(11)) multiplexer_9 (.in0(rom_7_data), .out(out_10), .sel(1'b0));  // open: in1, en
  ROM #(.addrWidth(4), .dataWidth(11)) rom_8 (.addr(counter_1_q), .data(rom_8_data));  // open: sel
  Multiplexer #(.width(11)) multiplexer_10 (.in0(rom_9_data), .out(out_11), .sel(1'b0));  // open: in1, en
  ROM #(.addrWidth(4), .dataWidth(11)) rom_9 (.addr(counter_1_q), .data(rom_9_data));  // open: sel
  ROM #(.addrWidth(4), .dataWidth(11)) rom_10 (.addr(counter_1_q), .data(rom_10_data));  // open: sel
  Multiplexer #(.width(11)) multiplexer_11 (.in0(rom_11_data), .out(out_12), .sel(1'b0));  // open: in1, en
  Multiplexer #(.width(11)) multiplexer_12 (.in0(rom_10_data), .out(out_6), .sel(1'b0));  // open: in1, en
  ROM #(.addrWidth(4), .dataWidth(11)) rom_11 (.addr(counter_1_q), .data(rom_11_data));  // open: sel

  // Notes on the sheet:
  //   contents of rom_1 (hex, n*v repeats v):
  //   4*0 20 202 505 505
  //   contents of rom_2 (hex, n*v repeats v):
  //   4*0 202 505
  //   contents of rom_3 (hex, n*v repeats v):
  //   0 0 0 104 20 202 505 505 104
  //   contents of rom_4 (hex, n*v repeats v):
  //   0 0 0 20 d8 0 0 88 88
  //   contents of rom_5 (hex, n*v repeats v):
  //   0 0 20 50 88 0 0 0 50
  //   contents of rom_6 (hex, n*v repeats v):
  //   0 20 50 88 505
  //   contents of rom_7 (hex, n*v repeats v):
  //   0 0 20 50 88 0 0 0 50
  //   contents of rom_8 (hex, n*v repeats v):
  //   0 0 0 20 d8 0 0 88 88
  //   contents of rom_9 (hex, n*v repeats v):
  //   0 0 0 104 20 202 505 505 104
  //   contents of rom_10 (hex, n*v repeats v):
  //   4*0 202 505
  //   contents of rom_11 (hex, n*v repeats v):
  //   4*0 20 202 505 505
endmodule
